# Fritzing sketch gingerbreadrfid (saved by Fritzing 1.0.6)
breadboards: 1

parts:
  Part1 = Arduino Uno (Rev3)
  Mod1 = KY-019 5V Relay Module [package="Breakout board"]
  A1 = uhppote electric strike door lock
  V5 = DC Power [voltage=12V internal_resistance=0.1Ω]
  R1 = Resistor [tolerance=±5% resistance=100 package="2512 [SMD]"]
  R2 = Resistor [tolerance=±5% resistance=100 package="2512 [SMD]"]
  R3 = Resistor [tolerance=±5% resistance=100 package="2512 [SMD]"]
  U1 = MFRC RFID522 [chip_label="RFID RC522"]

nets:
  N1: Part1.D9_PWM, U1.connector6
  N2: Part1.D10_PWM/SS, U1.connector0
  N3: Part1.D11_PWM/MOSI, R1.Pin_0
  N4: Part1.D12/MISO, R2.Pin_0
  N5: Part1.D13/SCK, R3.Pin_0
  GND: Part1.GND, Mod1.-, U1.connector5
  N6: Part1.D3_PWM, Mod1.S
  3.3V: Part1.3V3, U1.connector7
  5V: Part1.5V, Mod1.+
  N7: Mod1.NC, A1.pin2
  N8: Mod1.Common, V5.V+
  N9: A1.pin1, V5.V-
  N10: R1.Pin_1, U1.connector2
  N11: R2.Pin_1, U1.connector3
  N12: R3.Pin_1, U1.connector1

notes:
  100 ohm resistors are added on the spi signal lines (MOSI/MISO/SCK) to make sure that spi can work across the long wire distance.
  Both david and I aren't really sure why this worked, this is what google recommended (something about reducing signal drop/reflection?). Makes enough sense that I tried it, but neither of us understand exactly why this worked
  Michael, 07/01/26

custom parts:
  KY-019 5V Relay Module: KY-019 5V Relay module, used to control AC circuits. (Special thanks to vanepp for fixing the PCB holes and other errors)
  uhppote electric strike door lock: UHPPOTE electric strike door lock.
