# Fritzing sketch gobolight (saved by Fritzing 1.0.6)
breadboards: 1

parts:
  Part1 = Arduino Uno (Rev3)
  Part2 = Ambient Light Sensor (TEMT6000 Breakout Board)
  LED1 = LEDs [package=led-0603]
  LED2 = LED - 5mm [color="Red (633nm)" current=0.030A package="5 mm [THT]"]
  R1 = Resistor [tolerance=±5% power=0.25W resistance=2.2k package=THT]
  R2 = Resistor [tolerance=±5% power=0.25W resistance=10k package=THT]
  R3 = Resistor [tolerance=±5% power=0.25W resistance=4.7k package=THT]
  S1 = Taiway 100-SP-X-T1 SPDT Miniature Toggle Switch [part_number=100-SP-X-T1-0-0-B1-M1 package=THT]

nets:
  N1: Part1.A0, Part2.S
  GND: Part1.GND, Part2.GND, LED1.C, LED2.cathode, R3.Pin_1
  N2: Part1.D2, LED2.anode
  N3: Part1.D3_PWM, LED1.A
  N4: Part1.D7, R1.Pin_0, R2.Pin_0
  5V: Part1.5V
  3.3V: Part2.VCC
  N5: R1.Pin_1, R3.Pin_0
  12V: S1.L1
