# Fritzing sketch ingredientscircuit (saved by Fritzing 1.0.5)
breadboards: 1

parts:
  Part1 = Arduino Uno (Rev3)
  flour_right = US-100 Ultrasonic Distance Sensor
  flour_wrong = US-100 Ultrasonic Distance Sensor
  sugar_right = US-100 Ultrasonic Distance Sensor
  sugar_wrong = US-100 Ultrasonic Distance Sensor
  ginger_right = US-100 Ultrasonic Distance Sensor
  ginger_wrong = US-100 Ultrasonic Distance Sensor
  Mod1 = KY-019 5V Relay Module [package="Breakout board"]
  door_EM = uhppote electric strike door lock
  V9 = DC Power [voltage=12V internal_resistance=0.1Ω]
  S1 = Reed switch [package=THT]
  Mod2 = KY-019 5V Relay Module [package="Breakout board"]
  reveal_EM = uhppote electric strike door lock
  V11 = DC Power [voltage=12V internal_resistance=0.1Ω]
  V12 = DC Power [voltage=12V internal_resistance=0.1Ω]
  JL012-13-5_1 = JL012-13-5.2 Lever (Limit) Switch SPDT + NO + NC [part_number=JL012-13-5.2]
  ingredient_release = uhppote electric strike door lock

nets:
  N1: Part1.D8, Mod1.S
  N2: Part1.D9_PWM, S1.pin_1
  N3: Part1.D10_PWM/SS, Mod2.S
  GND: Part1.GND, flour_right.GND, flour_right.GND-2, flour_wrong.GND, flour_wrong.GND-2, sugar_right.GND, sugar_right.GND-2, sugar_wrong.GND, sugar_wrong.GND-2, ginger_right.GND, ginger_right.GND-2, ginger_wrong.GND, Mod1.-, S1.pin_2, Mod2.-
  N4: Part1.D2, flour_right.TRIG, flour_right.ECHO
  N5: Part1.D3_PWM, flour_wrong.TRIG, flour_wrong.ECHO
  N6: Part1.D4, sugar_right.TRIG, sugar_right.ECHO
  N7: Part1.D5_PWM, sugar_wrong.TRIG, sugar_wrong.ECHO
  N8: Part1.D6_PWM, ginger_right.TRIG, ginger_right.ECHO
  N9: Part1.D7, ginger_wrong.TRIG, ginger_wrong.ECHO
  5V: Part1.5V, flour_right.VCC, flour_wrong.VCC, sugar_right.VCC, sugar_wrong.VCC, ginger_right.VCC, ginger_wrong.VCC, Mod1.+, Mod2.+
  N10: Mod1.Common, V9.V+
  N11: Mod1.NO, door_EM.pin1
  N12: door_EM.pin2, V9.V-
  N13: Mod2.NC, reveal_EM.pin1
  N14: Mod2.Common, V11.V+
  N15: reveal_EM.pin2, V11.V-
  N16: V12.V-, ingredient_release.pin1
  N17: V12.V+, JL012-13-5_1.C
  N18: JL012-13-5_1.NC, ingredient_release.pin2

custom parts:
  KY-019 5V Relay Module: KY-019 5V Relay module, used to control AC circuits. (Special thanks to vanepp for fixing the PCB holes and other errors)
  uhppote electric strike door lock: UHPPOTE electric strike door lock.
  JL012-13-5.2 Lever (Limit) Switch SPDT + NO + NC: Micro Switch; Model No.: JL012-13.5-2; Actuator Action: Momentary; Actuator Type: Hinge Lever; Contact Configuration: 1NO, 1NC (SPDT) Temperature -25~65℃；Relative humidity: below 85%; Rate Voltage: 125V AC; Rated Current: 1A.
