# Fritzing sketch keypad puzzle (saved by Fritzing 1.0.6)
breadboards: 1

parts:
  R2 = Resistor [tolerance=±5% power=0.25W resistance=220 package=THT]
  R3 = Resistor [tolerance=±5% power=0.25W resistance=220 package=THT]
  Arduino_Mega_2560 = Arduino Mega 2560 (Rev3)
  kEYPAD_MATRICIAL_1 = KEYPAD 4x3
  R1 = Resistor [tolerance=±5% power=0.25W resistance=220 package=THT]
  U1 = 7-SEGMENT-4DIGIT [package=7-segment-4digit-youngsun]
  R4 = Resistor [tolerance=±5% power=0.25W resistance=220 package=THT]
  J1 = Piezo Speaker
  U2 = RELAY [package=relay-jzc]

nets:
  N1: R2.Pin_0, U1.8
  N2: R2.Pin_1, Arduino_Mega_2560.D6_PWM
  N3: R3.Pin_0, U1.9
  N4: R3.Pin_1, Arduino_Mega_2560.D5_PWM
  N5: Arduino_Mega_2560.D13_PWM, U1.1
  N6: Arduino_Mega_2560.D12_PWM, U1.2
  N7: Arduino_Mega_2560.D11_PWM, U1.3
  N8: Arduino_Mega_2560.D10_PWM, U1.4
  N9: Arduino_Mega_2560.D9_PWM, U1.5
  N10: Arduino_Mega_2560.D8_PWM, R1.Pin_1
  N11: Arduino_Mega_2560.GND, J1.pin1, U2.COIL2
  N12: Arduino_Mega_2560.D2_PWM, R4.Pin_1
  N13: Arduino_Mega_2560.D3_PWM, U1.13
  N14: Arduino_Mega_2560.D4_PWM, U1.11
  N15: Arduino_Mega_2560.D7_PWM, U1.7
  N16: Arduino_Mega_2560.D22, U2.COIL1
  N17: Arduino_Mega_2560.D40, kEYPAD_MATRICIAL_1.col1
  N18: Arduino_Mega_2560.D42, kEYPAD_MATRICIAL_1.arrow1
  N19: Arduino_Mega_2560.D44, kEYPAD_MATRICIAL_1.col2
  N20: Arduino_Mega_2560.D46, kEYPAD_MATRICIAL_1.arrow2
  N21: Arduino_Mega_2560.D48, kEYPAD_MATRICIAL_1.col3
  N22: Arduino_Mega_2560.D50, kEYPAD_MATRICIAL_1.arrow3
  N23: Arduino_Mega_2560.D52, kEYPAD_MATRICIAL_1.arrow4
  N24: Arduino_Mega_2560.D53, J1.pin2
  N25: R1.Pin_0, U1.6
  N26: U1.14, R4.Pin_0

notes:
  Pin positions on the 7--segment display depicted do not exactly match the model in use. Use the pinout on the schematic to understand how to connect it.
  This model shows 14 pins total, whereas ours has 12 pins total.
  So that it lines up on the schematic, the top wires here and the rightmost wire on the bottom are not in the correct positions per the physical component.
  Pins 13-8 on the arduino connect to the bottom row of pins (1-6) on the physical component.
  Pins 7-2 on the arduino connect to the top row of pins (12-7) on the physical component.
  The 7-segment display in use doesn't quite match this. Ours has 12 pins, not 14. The pinout shown here is correct.
  Note that D2 and D3 on the arduino depicted to the side have been swapped - this appears to be a bug with the Fritzing component. I've connected the pins correctly per the labels, so D2 PWM -> 12 and D3 PWM -> 11.
  More Fritzing weirdness with this relay, connected like this so it looks correct in the schematic, this is apparently the other end of the coil pin. Use the schematic to work out wiring, not this breadboard diagram.

custom parts:
  KEYPAD 4x3: KEYPAD matricial de 12 botones, 4 filas x 3 columnas
