# Fritzing sketch simonsays (saved by Fritzing 1.0.5)
breadboards: 1

parts:
  Part1 = Arduino Uno (Rev3) - ICSP
  LED5 = RGB LED (com. cathode, rgb) [color="Red (633nm)" current=0.030A package="5 mm [THT]"]
  R1 = Resistor [tolerance=±5% resistance=330 package="0805 [SMD]"]
  R2 = Resistor [tolerance=±5% resistance=330 package="0805 [SMD]"]
  R3 = Resistor [tolerance=±5% resistance=330 package="0805 [SMD]"]
  LED6 = RGB LED (com. cathode, rgb) [color="Red (633nm)" current=0.030A package="5 mm [THT]"]
  R4 = Resistor [tolerance=±5% resistance=330 package="0805 [SMD]"]
  R5 = Resistor [tolerance=±5% resistance=330 package="0805 [SMD]"]
  R6 = Resistor [tolerance=±5% resistance=330 package="0805 [SMD]"]
  LED7 = RGB LED (com. cathode, rgb) [color="Red (633nm)" current=0.030A package="5 mm [THT]"]
  R7 = Resistor [tolerance=±5% resistance=330 package="0805 [SMD]"]
  R8 = Resistor [tolerance=±5% resistance=330 package="0805 [SMD]"]
  R9 = Resistor [tolerance=±5% resistance=330 package="0805 [SMD]"]
  LED8 = RGB LED (com. cathode, rgb) [color="Red (633nm)" current=0.030A package="5 mm [THT]"]
  R10 = Resistor [tolerance=±5% resistance=330 package="0805 [SMD]"]
  R11 = Resistor [tolerance=±5% resistance=330 package="0805 [SMD]"]
  R12 = Resistor [tolerance=±5% resistance=330 package="0805 [SMD]"]
  JL012-13-5_1 = JL012-13-5.2 Lever (Limit) Switch SPDT + NO + NC [part_number=JL012-13-5.2]
  LED9 = smd LED [color="Red (633nm)" package="0805 [SMD]"]
  Part2 = Arduino Uno (Rev3) - ICSP
  Mod1 = KY-019 5V Relay Module [package="Breakout board"]
  JL012-13-5_2 = JL012-13-5.2 Lever (Limit) Switch SPDT + NO + NC [part_number=JL012-13-5.2]
  LED10 = smd LED [color="Green (560nm)" package="0805 [SMD]"]
  LED11 = smd LED [color="Blue (470nm)" package="0805 [SMD]"]
  LED12 = smd LED [color="Yellow (585nm)" package="0805 [SMD]"]
  JL012-13-5_3 = JL012-13-5.2 Lever (Limit) Switch SPDT + NO + NC [part_number=JL012-13-5.2]
  JL012-13-5_4 = JL012-13-5.2 Lever (Limit) Switch SPDT + NO + NC [part_number=JL012-13-5.2]
  A1 = Raspberry Pi 5
  A2 = uhppote electric strike door lock
  V4 = DC Power [voltage=12V]
  R13 = Resistor [tolerance=±5% resistance=330 package="0805 [SMD]"]
  R14 = Resistor [tolerance=±5% resistance=330 package="0805 [SMD]"]
  R15 = Resistor [tolerance=±5% resistance=330 package="0805 [SMD]"]
  R16 = Resistor [tolerance=±5% resistance=330 package="0805 [SMD]"]

nets:
  N1: Part1.ICSP_MISO, Part1.D12/MISO, R2.Pin_0
  N2: Part1.ICSP_SCK, Part1.D13/SCK, R3.Pin_0
  N3: Part1.ICSP_MOSI, Part1.D11_PWM/MOSI, R1.Pin_0
  GND: Part1.GND, LED5.common_cathode, LED6.common_cathode, LED7.common_cathode, LED8.common_cathode, JL012-13-5_1.C, Part2.GND, Mod1.-, JL012-13-5_2.C, JL012-13-5_3.C, JL012-13-5_4.C
  N4: Part1.D8, R6.Pin_0
  N5: Part1.D9_PWM, R5.Pin_0
  N6: Part1.D10_PWM/SS, R4.Pin_0
  N7: Part1.D0/RX, Part2.D0/RX, A1.GPIO26
  N8: Part1.D2, R11.Pin_0
  N9: Part1.D3_PWM, R10.Pin_0
  N10: Part1.D4, R12.Pin_0
  N11: Part1.D5_PWM, R8.Pin_0
  N12: Part1.D6_PWM, R9.Pin_0
  N13: Part1.D7, R7.Pin_0
  N14: LED5.red_anode, R3.Pin_1
  N15: LED5.green_anode, R2.Pin_1
  N16: LED5.blue_anode, R1.Pin_1
  N17: LED6.red_anode, R4.Pin_1
  N18: LED6.green_anode, R5.Pin_1
  N19: LED6.blue_anode, R6.Pin_1
  N20: LED7.red_anode, R7.Pin_1
  N21: LED7.green_anode, R9.Pin_1
  N22: LED7.blue_anode, R8.Pin_1
  N23: LED8.red_anode, R12.Pin_1
  N24: LED8.green_anode, R10.Pin_1
  N25: LED8.blue_anode, R11.Pin_1
  N26: JL012-13-5_1.NO, LED9.cathode, Part2.D2
  N27: LED9.anode, R13.Pin_1
  N28: Part2.ICSP_MISO, Part2.D12/MISO, Mod1.S
  5V: Part2.5V, Mod1.+, R13.Pin_0, R14.Pin_0, R15.Pin_0, R16.Pin_0
  N29: Part2.D8, LED12.cathode, JL012-13-5_4.NO
  N30: Part2.D4, JL012-13-5_2.NO, LED10.cathode
  N31: Part2.D6_PWM, LED11.cathode, JL012-13-5_3.NO
  N32: Mod1.NC, A2.pin1
  N33: Mod1.Common, V4.V+
  N34: LED10.anode, R14.Pin_1
  N35: LED11.anode, R15.Pin_1
  N36: LED12.anode, R16.Pin_1
  N37: A2.pin2, V4.V-

custom parts:
  JL012-13-5.2 Lever (Limit) Switch SPDT + NO + NC: Micro Switch; Model No.: JL012-13.5-2; Actuator Action: Momentary; Actuator Type: Hinge Lever; Contact Configuration: 1NO, 1NC (SPDT) Temperature -25~65℃；Relative humidity: below 85%; Rate Voltage: 125V AC; Rated Current: 1A.
  KY-019 5V Relay Module: KY-019 5V Relay module, used to control AC circuits. (Special thanks to vanepp for fixing the PCB holes and other errors)
  Raspberry Pi 5: The RPi5, a faster version of the awesome Raspberry Pi4B ARM Board with 40 pin gpio.
  uhppote electric strike door lock: UHPPOTE electric strike door lock.
