# Fritzing sketch Breakfast (saved by Fritzing 0.9.4)

parts:
  Part1 = Arduino Nano (Rev3.0)
  Part2 = RFID-RC522-v3
  Maglock = Camdenboss CTB0158-2 [part_number=CTB0158-2 package=THT]
  J3 = Camdenboss CTB0158-6 [part_number=CTB0158-6 package=THT]
  J4 = Camdenboss CTB0158-6 [part_number=CTB0158-6 package=THT]
  Part3 = KY-019 5V Relay Module [package="Breakout board"]

nets:
  GND: Part1.GND, Part2.GND, J3.pin2
  N1: Part1.D2, J3.pin5
  N2: Part1.D9, Part2.RST
  N3: Part1.D10, Part2.SDA
  N4: Part1.D11/MOSI, Part2.MOSI
  N5: Part1.D12/MISO, Part2.MISO
  N6: Part1.VIN, J3.pin1
  N7: Part1.RESET, J3.pin3
  N8: Part1.5V, J3.pin4
  N9: Part1.A0, J3.pin6
  3V3: Part1.3V3, Part2.3.3V
  N10: Part1.D13/SCK, Part2.SCK
  N11: Maglock.pin1, Maglock.terminal_1, Part3.NO
  N12: Maglock.pin2, Maglock.terminal_2, J3.terminal_2, J4.pin5, J4.terminal_5, Part3.-
  N13: J3.terminal_1, J4.pin6, J4.terminal_6
  N14: J3.terminal_3, J4.pin4, J4.terminal_4
  N15: J3.terminal_4, Part3.+
  N16: J3.terminal_5, Part3.S
  N17: J3.terminal_6, J4.pin1, J4.terminal_1
  N18: J4.terminal_2, Part3.Common

notes:
  "Rm#2" Maglock
  From Switchboard

custom parts:
  RFID-RC522-v3: A simple China made RFID-RC522 Reader (6x4 cm); do check the pin labels, as this is a MFRC522 based clone.
  KY-019 5V Relay Module: KY-019 5V Relay module, used to control AC circuits.
