# Fritzing sketch CowInsemination (saved by Fritzing 0.9.4)
stripboards: 2

parts:
  Maglock = Camdenboss CTB0158-2 [part_number=CTB0158-2 package=THT]
  J4 = Camdenboss CTB0158-6 [part_number=CTB0158-6 package=THT]
  Part1 = Arduino Uno (Rev3)
  J5 = Camdenboss CTB0158-6 [part_number=CTB0158-6 package=THT]
  Part2 = KY-019 5V Relay Module [package="Breakout board"]
  Part4 = KY-018 Photoresistor Module [package="Breakout board"]
  Part3 = KY-008 Laser Transmitter Module [package="Breakout board"]

nets:
  N1: Maglock.terminal_1, Part2.NO
  N2: Maglock.terminal_2, Part1.GND, J5.pin5, Part2.-, Part4.-, Part3.-
  N3: J4.terminal_1, J5.terminal_6
  N4: J4.terminal_2, J5.terminal_5
  N5: J4.terminal_3, J5.terminal_4
  N6: J4.terminal_4, J5.terminal_3
  N7: J4.terminal_5, J5.pin2, J5.terminal_2
  N8: J4.terminal_6, J5.terminal_1
  N9: Part1.A0, J5.pin3
  N10: Part1.A1, Part4.S
  N11: Part1.D8, Part3.S
  N12: Part1.D12/MISO, Part2.S
  N13: Part1.3V3, J5.pin6
  N14: Part1.5V, Part2.+, Part3.+
  N15: Part1.VIN, J5.pin4
  N16: J5.pin1, Part2.Common

notes:
  "Panel_R" Maglock
  From Switchboard

custom parts:
  KY-019 5V Relay Module: KY-019 5V Relay module, used to control AC circuits.
  KY-018 Photoresistor Module: KY-018 Photoresistor module, used to measure light intensity. It can determine the presence or absence of light.
  KY-008 Laser Transmitter Module: Laser Transmitter module KY-008 for Arduino, emits a dot shaped red laser beam.
