# Fritzing sketch TheFarm (saved by Fritzing 0.9.4)
stripboards: 2

parts:
  J4 = Camdenboss CTB0158-6 [part_number=CTB0158-6 package=THT]
  Part1 = Arduino Uno (Rev3)
  J5 = Camdenboss CTB0158-6 [part_number=CTB0158-6 package=THT]
  Part2 = KY-019 5V Relay Module [package="Breakout board"]
  Part3 = HX711 Weighing Sensor Module
  S1 = Square Pushbutton
  Part4 = KY-019 5V Relay Module [package="Breakout board"]
  Maglock2 = Camdenboss CTB0158-2 [part_number=CTB0158-2 package=THT]
  Maglock = Camdenboss CTB0158-2 [part_number=CTB0158-2 package=THT]
  Maglock3 = Camdenboss CTB0158-6 [part_number=CTB0158-6 package=THT]
  Maglock4 = Camdenboss CTB0158-4 [part_number=CTB0158-4 package=THT]
  R1 = Rotary Potentiometer (Large) [maximum_resistance=100kΩ package=THT]
  R2 = Rotary Potentiometer (Large) [maximum_resistance=100kΩ package=THT]

nets:
  N1: J4.terminal_1, Part1.RESET, J5.pin6
  GND: J4.terminal_2, Part1.GND, J5.pin5, Part3.GND, S1.leg0, Maglock2.terminal_1, Maglock.terminal_2
  N2: J4.terminal_3, Part1.VIN, J5.pin4, Part4.Common
  N3: J4.terminal_4, Part1.A0, J5.pin3
  N4: J4.terminal_5, J5.pin2, J5.terminal_2, Part4.NC
  N5: J4.terminal_6, J5.pin1, Part2.Common
  N6: Part1.D8, Part3.CK/TX
  N7: Part1.D9_PWM, Part3.DO/RX
  N8: Part1.D11_PWM/MOSI, S1.leg1
  N9: Part1.D12/MISO, Part4.S
  N10: Part1.D13/SCK, Part2.S
  N11: Part1.3V3, Maglock2.terminal_2
  5V: Part1.5V, Part3.VCC
  N12: Part2.+, Part4.+
  N13: Part2.-, Part4.-
  N14: Part2.NC, Maglock.terminal_1
  N15: Part3.E+, Maglock4.terminal_4
  N16: Part3.E-, Maglock4.terminal_3
  N17: Part3.A+, Maglock4.terminal_2
  N18: Part3.A-, Maglock4.terminal_1
  N19: Maglock3.terminal_1, R2.leg2
  N20: Maglock3.terminal_2, R2.wiper
  N21: Maglock3.terminal_3, R2.leg1
  N22: Maglock3.terminal_4, R1.leg2
  N23: Maglock3.terminal_5, R1.wiper
  N24: Maglock3.terminal_6, R1.leg1

notes:
  12VDC Maglock
  From Switchboard
  Exit Door
  Relay
  Float Switch
  RC Tractor Controller (3.3V)
  1kg Load Cell
  Left
  Panel
  Relay
  Forward|Back
  Left|Right

custom parts:
  KY-019 5V Relay Module: KY-019 5V Relay module, used to control AC circuits.
